// Logisim project PiCPU.circ as structural Verilog: 1 circuit, main circuit main
module main (
);

  wire Clk, comparator_1_eq, NxInst, ProgramCounter_carry, Reset, Stop, undriven;
  wire [7:0] Inst;
  wire [15:0] bit_extender_1_out, CounterMemory_dout, multiplexer_1_out, ProgramData;
  wire [23:0] ProgramCounter_q;

  Pull_Resistor pull_resistor_1 (.node(Clk));
  Pull_Resistor pull_resistor_2 (.node(Reset));
  Pull_Resistor pull_resistor_3 (.node(NxInst));
  Register ProgramSelector (
    .D(ProgramData[15:8]), .en(undriven), .clk(Clk), .Q(ProgramCounter_q[23:16]), .clr(ProgramCounter_carry));
  RAM #(.clearpin("true"), .dataWidth(16)) CounterMemory (
    .addr(ProgramCounter_q[23:16]), .oe(1'b1), .clk(Clk), .din(ProgramCounter_q[15:0]),
    .dout(CounterMemory_dout), .clr(Reset));  // open: we
  Comparator comparator_1 (.a({8{1'b0}}), .b(ProgramCounter_q[23:16]), .eq(comparator_1_eq));  // open: gt, lt
  and and_1 (Stop, comparator_1_eq, ProgramCounter_carry, ~Reset);  // AND_Gate
  assign bit_extender_1_out = {{8{1'b0}}, ProgramData[7:0]};  // Bit_Extender bit_extender_1
  Counter #(.max('hffff), .ongoal("stay"), .width(16)) ProgramCounter (
    .clr(Reset), .load(undriven), .up(1'b1), .count(NxInst), .clk(Clk), .D(multiplexer_1_out),
    .carry(ProgramCounter_carry), .Q(ProgramCounter_q[15:0]));
  Multiplexer #(.width(16)) multiplexer_1 (
    .in0(CounterMemory_dout), .in1(bit_extender_1_out), .out(multiplexer_1_out));  // open: sel
  ROM #(.addrWidth(24), .dataWidth(24)) Program (.addr(ProgramCounter_q), .data({Inst, ProgramData}));
endmodule
